// Logisim project peripheral_8x8disp.circ as structural Verilog: 3 circuits, main circuit Disp_Adr_Test
module Disp_Adr_Test (
  input  [8:0] Address_Is,
  input  [8:0] Address_Should,
  output out_3
);

  wire [8:0] xnor_1_out;

  Pull_Resistor pull_resistor_1 (.node(Address_Is));
  assign xnor_1_out = ~(Address_Is ^ Address_Should);  // XNOR_Gate xnor_1, 9 bits wide
  and and_1 (out_3, xnor_1_out[0], xnor_1_out[1], xnor_1_out[2], xnor_1_out[3], xnor_1_out[4], xnor_1_out[5], xnor_1_out[6], xnor_1_out[7], xnor_1_out[8]);
endmodule

module Disp_Mem (
  input  [7:0] DBus_In,
  input  [8:0] RAMABus_In,
  input  RESET,
  input  CLK,
  input  RAM_W_ASync,
  input  RAM_R_ASync,
  output [7:0] ROW_0,
  output [7:0] ROW_1,
  output [7:0] ROW_2,
  output [7:0] ROW_3,
  output [7:0] ROW_4,
  output [7:0] ROW_5,
  output [7:0] ROW_6,
  output [7:0] ROW_7
);

  Disp_Mem_Cell disp_mem_cell_1 (
    .RESET(RESET), .CLK(CLK), .RAM_W_Async(RAM_W_ASync), .RAM_R_Async(RAM_R_ASync), .RAMABus_In(RAMABus_In),
    .ADR(9'h1f8), .DBus_Out(DBus_In), .VAL(ROW_0), .DBus_In(DBus_In));
  Disp_Mem_Cell disp_mem_cell_2 (
    .RESET(RESET), .CLK(CLK), .RAM_W_Async(RAM_W_ASync), .RAM_R_Async(RAM_R_ASync), .RAMABus_In(RAMABus_In),
    .ADR(9'h1f9), .DBus_Out(DBus_In), .VAL(ROW_1), .DBus_In(DBus_In));
  Disp_Mem_Cell disp_mem_cell_3 (
    .RESET(RESET), .CLK(CLK), .RAM_W_Async(RAM_W_ASync), .RAM_R_Async(RAM_R_ASync), .RAMABus_In(RAMABus_In),
    .ADR(9'h1fa), .DBus_Out(DBus_In), .VAL(ROW_2), .DBus_In(DBus_In));
  Disp_Mem_Cell disp_mem_cell_4 (
    .RESET(RESET), .CLK(CLK), .RAM_W_Async(RAM_W_ASync), .RAM_R_Async(RAM_R_ASync), .RAMABus_In(RAMABus_In),
    .ADR(9'h1fb), .DBus_Out(DBus_In), .VAL(ROW_3), .DBus_In(DBus_In));
  Disp_Mem_Cell disp_mem_cell_5 (
    .RESET(RESET), .CLK(CLK), .RAM_W_Async(RAM_W_ASync), .RAM_R_Async(RAM_R_ASync), .RAMABus_In(RAMABus_In),
    .ADR(9'h1fc), .DBus_Out(DBus_In), .VAL(ROW_4), .DBus_In(DBus_In));
  Disp_Mem_Cell disp_mem_cell_6 (
    .RESET(RESET), .CLK(CLK), .RAM_W_Async(RAM_W_ASync), .RAM_R_Async(RAM_R_ASync), .RAMABus_In(RAMABus_In),
    .ADR(9'h1fd), .DBus_Out(DBus_In), .VAL(ROW_5), .DBus_In(DBus_In));
  Disp_Mem_Cell disp_mem_cell_7 (
    .RESET(RESET), .CLK(CLK), .RAM_W_Async(RAM_W_ASync), .RAM_R_Async(RAM_R_ASync), .RAMABus_In(RAMABus_In),
    .ADR(9'h1fe), .DBus_Out(DBus_In), .VAL(ROW_6), .DBus_In(DBus_In));
  Disp_Mem_Cell disp_mem_cell_8 (
    .RESET(RESET), .CLK(CLK), .RAM_W_Async(RAM_W_ASync), .RAM_R_Async(RAM_R_ASync), .RAMABus_In(RAMABus_In),
    .ADR({9{1'b1}}), .DBus_Out(DBus_In), .VAL(ROW_7), .DBus_In(DBus_In));
endmodule

module Disp_Mem_Cell (
  input  [7:0] DBus_In,
  input  RESET,
  input  CLK,
  input  RAM_W_Async,
  input  RAM_R_Async,
  input  [8:0] RAMABus_In,
  input  [8:0] ADR,
  output [7:0] DBus_Out,
  output [7:0] VAL
);

  wire and_1_out, and_2_out, disp_adr_test_1_out_3;

  Disp_Adr_Test disp_adr_test_1 (.Address_Is(RAMABus_In), .Address_Should(ADR), .out_3(disp_adr_test_1_out_3));
  and and_1 (and_1_out, RAM_W_Async, disp_adr_test_1_out_3);
  and and_2 (and_2_out, RAM_R_Async, disp_adr_test_1_out_3);
  Register register_1 (.D(DBus_In), .en(and_1_out), .Q(VAL), .clk(CLK), .clr(RESET));
  assign DBus_Out = and_2_out ? VAL : 8'bz;  // Controlled_Buffer controlled_buffer_1
endmodule
