// Logisim project peripheral_IOLR.circ as structural Verilog: 2 circuits, main circuit IOLR_Adr_Test
module IOLR_Adr_Test (
  input  [8:0] Address_Is,
  input  [8:0] Address_Should,
  output out_3
);

  wire [8:0] xnor_1_out;

  Pull_Resistor pull_resistor_1 (.node(Address_Is));
  assign xnor_1_out = ~(Address_Is ^ Address_Should);  // XNOR_Gate xnor_1, 9 bits wide
  and and_1 (out_3, xnor_1_out[0], xnor_1_out[1], xnor_1_out[2], xnor_1_out[3], xnor_1_out[4], xnor_1_out[5], xnor_1_out[6], xnor_1_out[7], xnor_1_out[8]);
endmodule

module IOLR_Register (
  input  L_in,
  input  R_in,
  input  RAM_R_Async,
  input  [8:0] RAMABus_In,
  output [7:0] DBus_Out
);

  wire and_1_out, iolr_adr_test_1_out_3;
  wire [7:2] undriven;

  IOLR_Adr_Test iolr_adr_test_1 (.Address_Is(RAMABus_In), .Address_Should(9'h1f7), .out_3(iolr_adr_test_1_out_3));
  and and_1 (and_1_out, RAM_R_Async, iolr_adr_test_1_out_3);
  assign DBus_Out = and_1_out ? {undriven, R_in, L_in} : 8'bz;  // Controlled_Buffer controlled_buffer_1
endmodule
