// Logisim project psMCU.circ as structural Verilog: 32 circuits, main circuit main
module FullAdder (
  input  A,
  input  B,
  input  Cin,
  output Out,
  output Cout
);

  wire and_1_out, and_2_out, xor_1_out;

  xor xor_1 (xor_1_out, A, B);
  xor xor_2 (Out, xor_1_out, Cin);
  and and_1 (and_1_out, xor_1_out, Cin);
  and and_2 (and_2_out, B, A);
  or or_1 (Cout, and_1_out, and_2_out);
endmodule

module Complementer (
  input  [7:0] IN,
  input  C_IN,
  input  DO_CIN,
  output C_OUT,
  output [7:0] OUT
);

  wire and_2_out, and_3_out, and_4_out, and_5_out, and_6_out, and_7_out, and_8_out, multiplexer_1_out;
  wire [7:0] not_1_out;

  and and_1 (C_OUT, and_2_out, not_1_out[7]);
  and and_2 (and_2_out, and_3_out, not_1_out[6]);
  xor xor_1 (OUT[7], not_1_out[7], and_2_out);
  xor xor_2 (OUT[6], not_1_out[6], and_3_out);
  and and_3 (and_3_out, and_4_out, not_1_out[5]);
  xor xor_3 (OUT[5], not_1_out[5], and_4_out);
  assign not_1_out = ~IN;  // NOT_Gate not_1, 8 bits wide
  and and_4 (and_4_out, and_5_out, not_1_out[4]);
  xor xor_4 (OUT[4], not_1_out[4], and_5_out);
  and and_5 (and_5_out, and_6_out, not_1_out[3]);
  xor xor_5 (OUT[3], not_1_out[3], and_6_out);
  and and_6 (and_6_out, and_7_out, not_1_out[2]);
  and and_7 (and_7_out, and_8_out, not_1_out[1]);
  xor xor_6 (OUT[2], not_1_out[2], and_7_out);
  xor xor_7 (OUT[1], not_1_out[1], and_8_out);
  and and_8 (and_8_out, multiplexer_1_out, not_1_out[0]);
  xor xor_8 (OUT[0], not_1_out[0], multiplexer_1_out);
  Multiplexer #(.enable("false")) multiplexer_1 (.in0(1'b1), .in1(C_IN), .out(multiplexer_1_out), .sel(DO_CIN));
endmodule

module BarrelShifter (
  input  OE,
  input  [7:0] Register_A,
  input  Shift_In,
  input  R,
  input  [7:0] Operand_B,
  output [7:0] DBus_OUT
);

  wire multiplexer_1_out, multiplexer_2_out, multiplexer_3_out, multiplexer_4_out, multiplexer_6_out,
       multiplexer_7_out, multiplexer_8_out, multiplexer_9_out, multiplexer_10_out, multiplexer_12_out,
       multiplexer_13_out, multiplexer_14_out, multiplexer_16_out, multiplexer_17_out, multiplexer_18_out,
       multiplexer_19_out, multiplexer_21_out, multiplexer_22_out, multiplexer_23_out, multiplexer_24_out,
       multiplexer_26_out, multiplexer_27_out, multiplexer_28_out, multiplexer_29_out, multiplexer_31_out,
       multiplexer_32_out, multiplexer_33_out, multiplexer_34_out, multiplexer_36_out, multiplexer_37_out,
       multiplexer_38_out, multiplexer_39_out;
  wire [7:0] multiplexer_40_out;

  Multiplexer #(.enable("false")) multiplexer_1 (
    .in0(Register_A[7]), .in1(Register_A[0]), .out(multiplexer_1_out), .sel(R));
  Multiplexer #(.enable("false")) multiplexer_2 (
    .in0(multiplexer_1_out), .in1(multiplexer_6_out), .out(multiplexer_2_out), .sel(Operand_B[0]));
  Multiplexer #(.enable("false")) multiplexer_3 (
    .in0(multiplexer_2_out), .in1(multiplexer_12_out), .out(multiplexer_3_out), .sel(Operand_B[1]));
  Multiplexer #(.enable("false")) multiplexer_4 (
    .in0(multiplexer_3_out), .in1(multiplexer_23_out), .out(multiplexer_4_out), .sel(Operand_B[2]));
  Multiplexer #(.enable("false")) multiplexer_5 (
    .in0(multiplexer_4_out), .in1(multiplexer_39_out), .out(multiplexer_40_out[7]), .sel(R));
  Multiplexer #(.enable("false")) multiplexer_6 (
    .in0(Register_A[6]), .in1(Register_A[1]), .out(multiplexer_6_out), .sel(R));
  Multiplexer #(.enable("false")) multiplexer_7 (
    .in0(multiplexer_6_out), .in1(multiplexer_10_out), .out(multiplexer_7_out), .sel(Operand_B[0]));
  Multiplexer #(.enable("false")) multiplexer_8 (
    .in0(multiplexer_7_out), .in1(multiplexer_17_out), .out(multiplexer_8_out), .sel(Operand_B[1]));
  Multiplexer #(.enable("false")) multiplexer_9 (
    .in0(multiplexer_8_out), .in1(multiplexer_28_out), .out(multiplexer_9_out), .sel(Operand_B[2]));
  Multiplexer #(.enable("false")) multiplexer_10 (
    .in0(Register_A[5]), .in1(Register_A[2]), .out(multiplexer_10_out), .sel(R));
  Multiplexer #(.enable("false")) multiplexer_11 (
    .in0(multiplexer_9_out), .in1(multiplexer_34_out), .out(multiplexer_40_out[6]), .sel(R));
  assign DBus_OUT = OE ? multiplexer_40_out : 8'bz;  // Controlled_Buffer controlled_buffer_1
  Multiplexer #(.enable("false")) multiplexer_12 (
    .in0(multiplexer_10_out), .in1(multiplexer_16_out), .out(multiplexer_12_out), .sel(Operand_B[0]));
  Multiplexer #(.enable("false")) multiplexer_13 (
    .in0(multiplexer_12_out), .in1(multiplexer_22_out), .out(multiplexer_13_out), .sel(Operand_B[1]));
  Multiplexer #(.enable("false")) multiplexer_14 (
    .in0(multiplexer_13_out), .in1(multiplexer_33_out), .out(multiplexer_14_out), .sel(Operand_B[2]));
  Multiplexer #(.enable("false")) multiplexer_15 (
    .in0(multiplexer_14_out), .in1(multiplexer_29_out), .out(multiplexer_40_out[5]), .sel(R));
  Multiplexer #(.enable("false")) multiplexer_16 (
    .in0(Register_A[4]), .in1(Register_A[3]), .out(multiplexer_16_out), .sel(R));
  Multiplexer #(.enable("false")) multiplexer_17 (
    .in0(multiplexer_16_out), .in1(multiplexer_21_out), .out(multiplexer_17_out), .sel(Operand_B[0]));
  Multiplexer #(.enable("false")) multiplexer_18 (
    .in0(multiplexer_17_out), .in1(multiplexer_27_out), .out(multiplexer_18_out), .sel(Operand_B[1]));
  Multiplexer #(.enable("false")) multiplexer_19 (
    .in0(multiplexer_18_out), .in1(multiplexer_38_out), .out(multiplexer_19_out), .sel(Operand_B[2]));
  Multiplexer #(.enable("false")) multiplexer_20 (
    .in0(multiplexer_19_out), .in1(multiplexer_24_out), .out(multiplexer_40_out[4]), .sel(R));
  Multiplexer #(.enable("false")) multiplexer_21 (
    .in0(Register_A[3]), .in1(Register_A[4]), .out(multiplexer_21_out), .sel(R));
  Multiplexer #(.enable("false")) multiplexer_22 (
    .in0(multiplexer_21_out), .in1(multiplexer_26_out), .out(multiplexer_22_out), .sel(Operand_B[0]));
  Multiplexer #(.enable("false")) multiplexer_23 (
    .in0(multiplexer_22_out), .in1(multiplexer_32_out), .out(multiplexer_23_out), .sel(Operand_B[1]));
  Multiplexer #(.enable("false")) multiplexer_24 (
    .in0(multiplexer_23_out), .in1(Shift_In), .out(multiplexer_24_out), .sel(Operand_B[2]));
  Multiplexer #(.enable("false")) multiplexer_25 (
    .in0(multiplexer_24_out), .in1(multiplexer_19_out), .out(multiplexer_40_out[3]), .sel(R));
  Multiplexer #(.enable("false")) multiplexer_26 (
    .in0(Register_A[2]), .in1(Register_A[5]), .out(multiplexer_26_out), .sel(R));
  Multiplexer #(.enable("false")) multiplexer_27 (
    .in0(multiplexer_26_out), .in1(multiplexer_31_out), .out(multiplexer_27_out), .sel(Operand_B[0]));
  Multiplexer #(.enable("false")) multiplexer_28 (
    .in0(multiplexer_27_out), .in1(multiplexer_37_out), .out(multiplexer_28_out), .sel(Operand_B[1]));
  Multiplexer #(.enable("false")) multiplexer_29 (
    .in0(multiplexer_28_out), .in1(Shift_In), .out(multiplexer_29_out), .sel(Operand_B[2]));
  Multiplexer #(.enable("false")) multiplexer_30 (
    .in0(multiplexer_29_out), .in1(multiplexer_14_out), .out(multiplexer_40_out[2]), .sel(R));
  Multiplexer #(.enable("false")) multiplexer_31 (
    .in0(Register_A[1]), .in1(Register_A[6]), .out(multiplexer_31_out), .sel(R));
  Multiplexer #(.enable("false")) multiplexer_32 (
    .in0(multiplexer_31_out), .in1(multiplexer_36_out), .out(multiplexer_32_out), .sel(Operand_B[0]));
  Multiplexer #(.enable("false")) multiplexer_33 (
    .in0(multiplexer_32_out), .in1(Shift_In), .out(multiplexer_33_out), .sel(Operand_B[1]));
  Multiplexer #(.enable("false")) multiplexer_34 (
    .in0(multiplexer_33_out), .in1(Shift_In), .out(multiplexer_34_out), .sel(Operand_B[2]));
  Multiplexer #(.enable("false")) multiplexer_35 (
    .in0(multiplexer_34_out), .in1(multiplexer_9_out), .out(multiplexer_40_out[1]), .sel(R));
  Multiplexer #(.enable("false")) multiplexer_36 (
    .in0(Register_A[0]), .in1(Register_A[7]), .out(multiplexer_36_out), .sel(R));
  Multiplexer #(.enable("false")) multiplexer_37 (
    .in0(multiplexer_36_out), .in1(Shift_In), .out(multiplexer_37_out), .sel(Operand_B[0]));
  Multiplexer #(.enable("false")) multiplexer_38 (
    .in0(multiplexer_37_out), .in1(Shift_In), .out(multiplexer_38_out), .sel(Operand_B[1]));
  Multiplexer #(.enable("false")) multiplexer_39 (
    .in0(multiplexer_38_out), .in1(Shift_In), .out(multiplexer_39_out), .sel(Operand_B[2]));
  Multiplexer #(.enable("false")) multiplexer_40 (
    .in0(multiplexer_39_out), .in1(multiplexer_4_out), .out(multiplexer_40_out[0]), .sel(R));
endmodule

module ALU (
  input  DO_C_in,
  input  C_in,
  input  [7:0] Register_A,
  input  [7:0] Operand_B,
  input  [7:0] RegB_Komplement,
  input  Do_B_Komp,
  input  OE,
  output [7:0] DBus_OUT,
  output HC,
  output C,
  output OVF
);

  wire and_1_out, and_2_out, and_3_out, fulladder_1_cout, fulladder_2_cout, fulladder_3_cout,
       fulladder_5_cout, fulladder_6_cout, fulladder_7_cout;
  wire [7:0] fulladder_1_out, multiplexer_1_out;

  Multiplexer #(.width(8), .enable("false")) multiplexer_1 (
    .in0(Operand_B), .in1(RegB_Komplement), .out(multiplexer_1_out), .sel(Do_B_Komp));
  and and_1 (and_1_out, DO_C_in, C_in);
  FullAdder fulladder_1 (
    .A(Register_A[0]), .B(multiplexer_1_out[0]), .Cin(and_1_out), .Out(fulladder_1_out[0]),
    .Cout(fulladder_1_cout));
  FullAdder fulladder_2 (
    .A(Register_A[1]), .B(multiplexer_1_out[1]), .Cin(fulladder_1_cout), .Out(fulladder_1_out[1]),
    .Cout(fulladder_2_cout));
  FullAdder fulladder_3 (
    .A(Register_A[2]), .B(multiplexer_1_out[2]), .Cin(fulladder_2_cout), .Out(fulladder_1_out[2]),
    .Cout(fulladder_3_cout));
  FullAdder fulladder_4 (
    .A(Register_A[3]), .B(multiplexer_1_out[3]), .Cin(fulladder_3_cout), .Out(fulladder_1_out[3]), .Cout(HC));
  FullAdder fulladder_5 (
    .A(Register_A[4]), .B(multiplexer_1_out[4]), .Cin(HC), .Out(fulladder_1_out[4]), .Cout(fulladder_5_cout));
  FullAdder fulladder_6 (
    .A(Register_A[5]), .B(multiplexer_1_out[5]), .Cin(fulladder_5_cout), .Out(fulladder_1_out[5]),
    .Cout(fulladder_6_cout));
  FullAdder fulladder_7 (
    .A(Register_A[6]), .B(multiplexer_1_out[6]), .Cin(fulladder_6_cout), .Out(fulladder_1_out[6]),
    .Cout(fulladder_7_cout));
  FullAdder fulladder_8 (
    .A(Register_A[7]), .B(multiplexer_1_out[7]), .Cin(fulladder_7_cout), .Out(fulladder_1_out[7]), .Cout(C));
  and and_2 (and_2_out, ~Register_A[7], ~multiplexer_1_out[7], fulladder_1_out[7]);  // AND_Gate
  or or_1 (OVF, and_2_out, and_3_out);
  and and_3 (and_3_out, Register_A[7], multiplexer_1_out[7], ~fulladder_1_out[7]);  // AND_Gate
  assign DBus_OUT = OE ? fulladder_1_out : 8'bz;  // Controlled_Buffer controlled_buffer_1
endmodule

module Temp_Reg (
  input  [7:0] DBUS_In,
  input  LATCH_L,
  input  LATCH_H,
  input  CLK,
  input  RESET,
  input  OE_ADR,
  input  OE_DATAL,
  output [7:0] DBG_L,
  output [7:0] DBUS_Out,
  output [13:0] ROMABus_Out,
  output [7:0] DBG_H
);

  Register register_1 (.D(DBUS_In), .en(LATCH_L), .Q(DBG_L), .clk(CLK), .clr(RESET));
  Register register_2 (.D(DBUS_In), .en(LATCH_H), .Q(DBG_H), .clk(CLK), .clr(RESET));
  assign DBUS_Out = OE_DATAL ? DBG_L : 8'bz;  // Controlled_Buffer controlled_buffer_1
  assign ROMABus_Out = OE_ADR ? {DBG_H[5:0], DBG_L} : 14'bz;  // Controlled_Buffer controlled_buffer_2
endmodule

module Logic (
  input  COMP_C_IN,
  input  [15:0] Inst,
  input  [7:0] Register_A,
  input  [7:0] Operand_B,
  input  COMP,
  input  NOT,
  input  DUAL_OP_OE,
  output COMP_C_OUT,
  output [7:0] Register_B_Complement,
  output [7:0] DBus_Out
);

  wire and_1_out, and_2_out, and_3_out, and_5_out, and_6_out, and_7_out, not_1_out, not_2_out;
  wire [7:0] and_4_out, not_3_out, or_1_out, xor_1_out;

  and and_1 (and_1_out, not_1_out, not_2_out);
  not not_1 (not_1_out, Inst[10]);
  not not_2 (not_2_out, Inst[9]);
  and and_2 (and_2_out, not_1_out, Inst[9]);
  and and_3 (and_3_out, Inst[10], not_2_out);
  assign not_3_out = ~Register_A;  // NOT_Gate not_3, 8 bits wide
  assign DBus_Out = NOT ? not_3_out : 8'bz;  // Controlled_Buffer controlled_buffer_1
  assign and_4_out = Register_A & Operand_B;  // AND_Gate and_4, 8 bits wide
  and and_5 (and_5_out, and_1_out, DUAL_OP_OE);
  assign DBus_Out = and_5_out ? and_4_out : 8'bz;  // Controlled_Buffer controlled_buffer_2
  assign or_1_out = Register_A | Operand_B;  // OR_Gate or_1, 8 bits wide
  and and_6 (and_6_out, and_2_out, DUAL_OP_OE);
  assign DBus_Out = and_6_out ? or_1_out : 8'bz;  // Controlled_Buffer controlled_buffer_3
  and and_7 (and_7_out, and_3_out, DUAL_OP_OE);
  assign xor_1_out = Register_A ^ Operand_B;  // XOR_Gate xor_1, 8 bits wide
  assign DBus_Out = and_7_out ? xor_1_out : 8'bz;  // Controlled_Buffer controlled_buffer_4
  Complementer complementer_1 (
    .IN(Operand_B), .OUT(Register_B_Complement), .C_OUT(COMP_C_OUT), .C_IN(COMP_C_IN), .DO_CIN(Inst[11]));
  assign DBus_Out = COMP ? Register_B_Complement : 8'bz;  // Controlled_Buffer controlled_buffer_5
endmodule

module Inst_Reg (
  input  [15:0] NextInst_Input,
  input  LATCH_EN,
  input  CLK,
  input  RESET,
  output [15:0] Inst_Output
);

  Register #(.width(16)) register_1 (.D(NextInst_Input), .en(LATCH_EN), .Q(Inst_Output), .clk(CLK), .clr(RESET));
endmodule

module ROM (
  input  [13:0] PC_VAL_IN,
  output [15:0] NextInst_OUT
);

  ROM_part #(.addrWidth(14), .dataWidth(16)) rom_1 (.addr(PC_VAL_IN), .data(NextInst_OUT), .sel(1'b1));

  // Notes on the sheet:
  //   contents of rom_1 (hex, n*v repeats v):
  //   c003 c002 3600 404 800d 100 40a 800d 100 412 800d 100 c003 6502 3700 3800 23ff 800d 200 3900 2200
  //   600 3700 100 c017
endmodule

module RAM (
  input  [7:0] DBus_In,
  input  [8:0] RAMABus_In,
  input  [6:0] Page_in,
  input  LatchSafeDA,
  input  Clk,
  input  RESET,
  input  Async_W,
  input  AsyncR_LatchSafeA,
  output [7:0] DBus_Out
);

  wire and_1_out, and_2_out, and_3_out, d_ff_1_q, d_ff_2_q, not_1_out, or_1_out, or_2_out;
  wire [7:0] controlled_buffer_1_out, register_1_q, register_2_q;

  Pull_Resistor pull_resistor_1 (.node(RAMABus_In[8]));
  not not_1 (not_1_out, RAMABus_In[8]);
  and and_1 (and_1_out, not_1_out, LatchSafeDA);
  and and_2 (and_2_out, Async_W, not_1_out);
  and and_3 (and_3_out, AsyncR_LatchSafeA, not_1_out);
  or or_1 (or_1_out, and_1_out, and_3_out);
  Register register_1 (.D(DBus_In), .en(and_1_out), .Q(register_1_q), .clk(Clk), .clr(RESET));
  Register register_2 (.D(RAMABus_In[7:0]), .en(or_1_out), .Q(register_2_q), .clk(Clk), .clr(RESET));
  D_Flip_Flop d_ff_1 (.clk(Clk), .D(and_2_out), .Q(d_ff_1_q), .reset(RESET));  // open: Qn, preset, en
  assign controlled_buffer_1_out = d_ff_2_q ? register_1_q : 8'bz;  // Controlled_Buffer controlled_buffer_1
  D_Flip_Flop d_ff_2 (.clk(Clk), .D(and_1_out), .Q(d_ff_2_q), .reset(RESET));  // open: Qn, preset, en
  or or_2 (or_2_out, d_ff_1_q, and_3_out);
  RAM_part #(.addrWidth(15), .bus("asynch")) ram_1 (
    .addr({Page_in, register_2_q}), .data(controlled_buffer_1_out), .sel(or_2_out), .ld(and_3_out),
    .clr(RESET));
  assign DBus_Out = and_3_out ? controlled_buffer_1_out : 8'bz;  // Controlled_Buffer controlled_buffer_2
endmodule

module PC (
  input  Latch_EN,
  input  [13:0] ROMABus_IN,
  input  INC_EN,
  input  CLK,
  input  RESET,
  input  CNDT_INC_ENT,
  input  Conditional_Affirmative,
  output [13:0] PC_VAL
);

  wire and_1_out, or_1_out;

  or or_1 (or_1_out, INC_EN, and_1_out);
  and and_1 (and_1_out, CNDT_INC_ENT, Conditional_Affirmative);
  Counter #(.width(14), .max('h3fff)) counter_1 (
    .load(Latch_EN), .D(ROMABus_IN), .count(or_1_out), .Q(PC_VAL), .clk(CLK), .clr(RESET));  // open: carry
endmodule

module Stack (
  input  CLK,
  input  RESET,
  input  [7:0] DATABUS_IN,
  input  Sync_Data,
  input  Present_Data,
  input  Ptr_Latch,
  input  Sync_Adr,
  input  Ofs_Sgn,
  input  Ofs_0,
  input  R,
  input  Ofs_1,
  input  Ofs__1,
  input  W,
  input  [15:0] Inst,
  output [14:0] DBG,
  output [7:0] DATABUS_OUT
);

  wire d_ff_1_q, d_ff_2_q, nor_1_out, or_1_out;
  wire [7:0] controlled_buffer_1_out, controlled_buffer_4_out, register_3_q;
  wire [14:0] adder_1_out, bit_extender_1_out, register_2_q;

  nor nor_1 (nor_1_out, Ofs__1, Ofs_1, Ofs_0);
  assign controlled_buffer_1_out = Ofs_1 ? 8'h1 : 8'bz;  // Controlled_Buffer controlled_buffer_1
  Pull_Resistor pull_resistor_1 (.node(controlled_buffer_1_out));
  assign controlled_buffer_1_out = Ofs__1 ? {8{1'b1}} : 8'bz;  // Controlled_Buffer controlled_buffer_2
  assign controlled_buffer_1_out = nor_1_out ? Inst[7:0] : 8'bz;  // Controlled_Buffer controlled_buffer_3
  Register #(.width(15)) register_1 (.D(adder_1_out), .en(Ptr_Latch), .Q(DBG), .clk(CLK), .clr(RESET));
  assign bit_extender_1_out = {{7{Ofs_Sgn}}, controlled_buffer_1_out};  // Bit_Extender bit_extender_1
  Adder #(.width(15)) adder_1 (.a(DBG), .b(bit_extender_1_out), .out(adder_1_out));  // open: cin, cout
  Register #(.width(15)) register_2 (.D(adder_1_out), .en(Sync_Adr), .Q(register_2_q), .clk(CLK), .clr(RESET));
  Register register_3 (.D(DATABUS_IN), .en(Sync_Data), .Q(register_3_q), .clk(CLK), .clr(RESET));
  D_Flip_Flop d_ff_1 (.clk(CLK), .D(W), .Q(d_ff_1_q), .reset(RESET));  // open: Qn, preset, en
  or or_1 (or_1_out, d_ff_1_q, R);
  assign controlled_buffer_4_out = d_ff_2_q ? register_3_q : 8'bz;  // Controlled_Buffer controlled_buffer_4
  D_Flip_Flop d_ff_2 (.clk(CLK), .D(Present_Data), .Q(d_ff_2_q), .reset(RESET));  // open: Qn, preset, en
  RAM_part #(.addrWidth(15), .bus("asynch")) ram_1 (
    .addr(register_2_q), .data(controlled_buffer_4_out), .sel(or_1_out), .ld(R), .clr(RESET));
  assign DATABUS_OUT = R ? controlled_buffer_4_out : 8'bz;  // Controlled_Buffer controlled_buffer_5
endmodule

module RegA (
  input  [7:0] DBus_IN,
  input  LATCH_EN,
  input  CLK,
  input  RESET,
  input  OE,
  output [7:0] DBus_Out,
  output [7:0] Value
);

  Register register_1 (.D(DBus_IN), .en(LATCH_EN), .Q(Value), .clk(CLK), .clr(RESET));
  assign DBus_Out = OE ? Value : 8'bz;  // Controlled_Buffer controlled_buffer_1
endmodule

module RegB (
  input  [7:0] DBus_IN,
  input  LATCH_EN,
  input  CLK,
  input  RESET,
  input  OE,
  output [7:0] DBus_Out,
  output [7:0] Value
);

  Register register_1 (.D(DBus_IN), .en(LATCH_EN), .Q(Value), .clk(CLK), .clr(RESET));
  assign DBus_Out = OE ? Value : 8'bz;  // Controlled_Buffer controlled_buffer_1
endmodule

module Adr_Test (
  input  [8:0] Address_Is,
  input  [8:0] Address_Should,
  output out_3
);

  wire [8:0] xnor_1_out;

  Pull_Resistor pull_resistor_1 (.node(Address_Is));
  assign xnor_1_out = ~(Address_Is ^ Address_Should);  // XNOR_Gate xnor_1, 9 bits wide
  and and_1 (out_3, xnor_1_out[0], xnor_1_out[1], xnor_1_out[2], xnor_1_out[3], xnor_1_out[4], xnor_1_out[5], xnor_1_out[6], xnor_1_out[7], xnor_1_out[8]);
endmodule

module SystemReg1 (
  input  Comp_OE,
  input  COMP_C_in,
  input  ALU_Comp_B,
  input  ALU_OE,
  input  OVF_in,
  input  RAM_W_Async,
  input  RAM_R_ASync,
  input  HC_in,
  input  [8:0] RAMABus_IN,
  input  C_in,
  input  [7:0] DBus_IN,
  input  CLK,
  input  RESET,
  output Comp_C_Out,
  output C_out,
  output ShiftIn,
  output [7:0] DBG,
  output [7:0] DBus_OUT
);

  wire adr_test_1_out_3, and_1_out, and_2_out, and_3_out, multiplexer_1_out, or_1_out, or_2_out, or_3_out;
  wire [2:0] multiplexer_4_out;

  and and_1 (and_1_out, ALU_Comp_B, ALU_OE);
  or or_1 (or_1_out, Comp_OE, and_1_out);
  and and_2 (and_2_out, adr_test_1_out_3, RAM_W_Async);
  and and_3 (and_3_out, RAM_R_ASync, adr_test_1_out_3);
  Adr_Test adr_test_1 (.Address_Is(RAMABus_IN), .Address_Should(9'h100), .out_3(adr_test_1_out_3));
  or or_2 (or_2_out, or_1_out, and_2_out);
  or or_3 (or_3_out, and_2_out, ALU_OE);
  Multiplexer #(.enable("false")) multiplexer_1 (
    .in0(DBus_IN[4]), .in1(COMP_C_in), .out(multiplexer_1_out), .sel(or_1_out));
  Multiplexer #(.enable("false")) multiplexer_2 (
    .in0(DBus_IN[3]), .in1(OVF_in), .out(multiplexer_4_out[2]), .sel(ALU_OE));
  Multiplexer #(.enable("false")) multiplexer_3 (
    .in0(DBus_IN[2]), .in1(HC_in), .out(multiplexer_4_out[1]), .sel(ALU_OE));
  Multiplexer #(.enable("false")) multiplexer_4 (
    .in0(DBus_IN[1]), .in1(C_in), .out(multiplexer_4_out[0]), .sel(ALU_OE));
  Register #(.width(1)) register_1 (.D(multiplexer_1_out), .en(or_2_out), .Q(Comp_C_Out), .clk(CLK), .clr(RESET));
  Register #(.width(3)) register_2 (
    .D(multiplexer_4_out), .en(or_3_out), .Q({DBG[3:2], C_out}), .clk(CLK), .clr(RESET));
  Register #(.width(1)) register_3 (.D(DBus_IN[0]), .en(and_2_out), .Q(DBG[0]), .clk(CLK), .clr(RESET));
  assign DBus_OUT = and_3_out ? {3'b000, Comp_C_Out, DBG[3:2], C_out, DBG[0]} : 8'bz;  // Controlled_Buffer controlled_buffer_1

  assign {DBG[7:4], DBG[1]} = {3'b000, Comp_C_Out, C_out};
  assign ShiftIn = DBG[0];

  // Notes on the sheet:
  //   Clock Freq.
endmodule

module SystemReg2 (
  input  [7:0] DBus_IN,
  input  RAM_W_Async,
  input  RAM_R_Async,
  input  [8:0] RAMABus_IN,
  input  CLK,
  input  RESET,
  output [7:0] DBG,
  output [7:0] DBus_Out,
  output [6:0] Ram_Page
);

  wire adr_test_1_out_3, and_1_out, and_2_out;

  and and_1 (and_1_out, adr_test_1_out_3, RAM_W_Async);
  and and_2 (and_2_out, RAM_R_Async, adr_test_1_out_3);
  Adr_Test adr_test_1 (.Address_Is(RAMABus_IN), .Address_Should(9'h101), .out_3(adr_test_1_out_3));
  Register #(.width(7)) register_1 (.D(DBus_IN[6:0]), .en(and_1_out), .Q(DBG[6:0]), .clk(CLK), .clr(RESET));
  assign DBus_Out = and_2_out ? {1'b0, DBG[6:0]} : 8'bz;  // Controlled_Buffer controlled_buffer_1

  assign DBG[7] = 1'b0;
  assign Ram_Page = DBG[6:0];
endmodule

module SystemReg3 (
  input  [7:0] DBus_IN,
  input  RAM_W_Async,
  input  RAM_R_Async,
  input  [8:0] RAMABus_IN,
  input  CLK,
  input  RESET,
  input  Set_Btn_Flag,
  input  [4:0] Comparison,
  output [7:0] DBG,
  output INT_EN,
  output [7:0] DBus_Out
);

  wire adr_test_1_out_3, and_1_out, and_2_out, or_1_out, or_2_out;

  and and_1 (and_1_out, adr_test_1_out_3, RAM_W_Async);
  and and_2 (and_2_out, RAM_R_Async, adr_test_1_out_3);
  Adr_Test adr_test_1 (.Address_Is(RAMABus_IN), .Address_Should(9'h102), .out_3(adr_test_1_out_3));
  or or_1 (or_1_out, DBus_IN[1], Set_Btn_Flag);
  or or_2 (or_2_out, Set_Btn_Flag, and_1_out);
  Register #(.width(1)) register_1 (.D(DBus_IN[0]), .en(and_1_out), .Q(DBG[0]), .clk(CLK), .clr(RESET));
  Register #(.width(1)) register_2 (.D(or_1_out), .en(or_2_out), .Q(DBG[1]), .clk(CLK), .clr(RESET));
  assign DBus_Out = and_2_out ? {1'b0, Comparison, DBG[1:0]} : 8'bz;  // Controlled_Buffer controlled_buffer_1

  assign DBG[7:2] = {1'b0, Comparison};
  assign INT_EN = DBG[0];

  // Notes on the sheet:
  //   Interrupt En Bit
  //   Btn Interrupt Flag
endmodule

module CrossOver (
  input  [15:0] Inst,
  input  [13:0] PC_Val,
  input  [7:0] RegB,
  input  Inst_0__13___ROMABus,
  input  PC_Val_0__7___DBus,
  input  PC_Val_8__13___DBus,
  input  Inst_0__8___RAMABus_0__8,
  input  Inst_0__8__RegB__RAMABus_0__8,
  input  Inst_0__7___DBus,
  input  INTAdr__ROMA,
  input  [13:0] Inst_Adr,
  input  InstAdr_0__7___DBus,
  input  InstAdr_8__13___DBus,
  output [13:0] ROMABus_Out,
  output [8:0] RAMABus_Out,
  output [7:0] DBus_Out,
  output [7:0] OperandB
);

  wire [8:0] adder_1_out;

  assign DBus_Out = InstAdr_0__7___DBus ? Inst_Adr[7:0] : 8'bz;  // Controlled_Buffer controlled_buffer_1
  assign DBus_Out = InstAdr_8__13___DBus ? {2'b00, Inst_Adr[13:8]} : 8'bz;  // Controlled_Buffer controlled_buffer_2
  Adder #(.width(9)) adder_1 (.a({1'b0, RegB}), .b(Inst[8:0]), .out(adder_1_out));  // open: cin, cout
  assign RAMABus_Out = Inst_0__8__RegB__RAMABus_0__8 ? adder_1_out : 9'bz;  // Controlled_Buffer controlled_buffer_3
  assign RAMABus_Out = Inst_0__8___RAMABus_0__8 ? Inst[8:0] : 9'bz;  // Controlled_Buffer controlled_buffer_4
  assign DBus_Out = PC_Val_0__7___DBus ? PC_Val[7:0] : 8'bz;  // Controlled_Buffer controlled_buffer_5
  assign DBus_Out = PC_Val_8__13___DBus ? {2'b00, PC_Val[13:8]} : 8'bz;  // Controlled_Buffer controlled_buffer_6
  assign DBus_Out = Inst_0__7___DBus ? Inst[7:0] : 8'bz;  // Controlled_Buffer controlled_buffer_7
  Multiplexer #(.width(8), .enable("false")) multiplexer_1 (.in0(RegB), .in1(Inst[7:0]), .out(OperandB), .sel(Inst[8]));
  assign ROMABus_Out = INTAdr__ROMA ? 14'h1 : 14'bz;  // Controlled_Buffer controlled_buffer_8
  assign ROMABus_Out = Inst_0__13___ROMABus ? Inst[13:0] : 14'bz;  // Controlled_Buffer controlled_buffer_9
endmodule

module Comparison (
  input  [7:0] A,
  input  [7:0] B,
  output [4:0] Comparison1
);

  Comparator #(.mode("unsigned")) comparator_1 (
    .a(A), .b(B), .gt(Comparison1[3]), .eq(Comparison1[2]), .lt(Comparison1[4]));
  nor nor_1 (Comparison1[0], A[0], A[1], A[2], A[3], A[4], A[5], A[6], A[7]);
  nor nor_2 (Comparison1[1], B[0], B[1], B[2], B[3], B[4], B[5], B[6], B[7]);
endmodule

module Control (
  input  [15:0] INST,
  input  INT_EN,
  input  INT,
  input  CLK,
  input  RESET,
  input  BreakPoint,
  input  DO_STEP_INST,
  input  STEP_INST,
  output [7:0] CTRL_BUS_0,
  output [7:0] CTRL_BUS_1,
  output Int__Active,
  output [7:0] CTRL_BUS_2,
  output [7:0] CTRL_BUS_3,
  output [7:0] CTRL_BUS_4,
  output [8:0] DBG,
  output [7:0] CTRL_BUS_5
);

  wire and_1_out, comparator_1_eq, not_1_out;
  wire [7:0] rom_3_data;
  wire [8:8] interrupt_control_1_int_noverride;

  Interrupt_Control interrupt_control_1 (
    .Assert(INT), .Int__Enabled(INT_EN), .InstR_Latch(CTRL_BUS_0[4]), .Int__Clr(CTRL_BUS_5[4]), .Clk(CLK),
    .Reset(RESET), .Int_Active(Int__Active), .Int_nOverride(interrupt_control_1_int_noverride[8]),
    .Int__Override_Clr(CTRL_BUS_5[5]));
  Comparator #(.width(3)) comparator_1 (.a(3'b000), .b(DBG[2:0]), .eq(comparator_1_eq));  // open: gt, lt
  Halt_Control halt_control_1 (
    .Bkpt(BreakPoint), .SubInst_0(comparator_1_eq), .Halt_Set(CTRL_BUS_0[2]), .Halt_Clr(CTRL_BUS_0[3]),
    .CLK(CLK), .RESET(RESET), .Halted(DBG[8]), .Step(STEP_INST), .Step_EN(DO_STEP_INST));
  not not_1 (not_1_out, CTRL_BUS_0[1]);
  and and_1 (and_1_out, not_1_out, CTRL_BUS_0[0]);
  ROM_part #(.addrWidth(9), .dataWidth(5)) rom_1 (
    .addr({interrupt_control_1_int_noverride[8], INST[15:8]}), .data(DBG[7:3]), .sel(1'b1));
  Counter #(.width(3), .max('h7)) counter_1 (
    .load(CTRL_BUS_0[1]), .D(3'b000), .count(and_1_out), .Q(DBG[2:0]), .clk(CLK), .clr(RESET));  // open: carry
  ROM_part #(.addrWidth(9)) rom_2 (.addr(DBG), .data(CTRL_BUS_0), .sel(1'b1));
  ROM_part #(.addrWidth(9)) rom_3 (.addr(DBG), .data(rom_3_data), .sel(1'b1));
  ROM_part #(.addrWidth(9)) rom_4 (.addr(DBG), .data(CTRL_BUS_2), .sel(1'b1));
  ROM_part #(.addrWidth(9)) rom_5 (.addr(DBG), .data(CTRL_BUS_3), .sel(1'b1));
  ROM_part #(.addrWidth(9)) rom_6 (.addr(DBG), .data(CTRL_BUS_4), .sel(1'b1));
  ROM_part #(.addrWidth(9)) rom_7 (.addr(DBG), .data(CTRL_BUS_5), .sel(1'b1));
  RegAB_Switch regab_switch_1 (.Bus_In(rom_3_data), .Inst(INST), .Bus_Out(CTRL_BUS_1));

  // Notes on the sheet:
  //   Instruction Decode ROM
  //   SubInstr Counter
  //   Make sure +1 is OFF
  //   when we load
  //   contents of rom_1 (hex, n*v repeats v):
  //   1e 1d 1c 1b 1a 1e 1a 1e 19 19 18 18 4*17 4*16 1e 15 14 14 8*13 12 12 11 11 f 10 e e 12 12 11 11 f 10
  //   d d c b c b a 9 6 5 8 7 8 7 5*1e 4 1e 4 1e 4 1e 4 1e 4 1e 4 1e 4 1e 4 1e 4 1e 4 1e 4 1e 4 1e 4 1e 4
  //   1e 4 1e 4 32*3 64*2 64*1
  //   MicroCode  ROM 0
  //   MicroCode  ROM 1
  //   MicroCode  ROM 2
  //   MicroCode  ROM 3
  //   MicroCode  ROM 4
  //   MicroCode  ROM 5
  //   contents of rom_2 (hex, n*v repeats v):
  //   5*1 81 32 0 81 32 6*0 5*1 81 32 0 1 41 32 5*0 41 32 6*0 1 1 1 81 32 0 0 0 1 1 1 81 32 0 0 0 1 32 6*0
  //   1 1 32 5*0 32 7*0 32 7*0 1 32 6*0 1 1 32 5*0 1 1 1 32 4*0 1 1 32 5*0 32 7*0 1 1 1 32 4*0 32 7*0 32
  //   7*0 32 7*0 32 7*0 32 7*0 1 1 32 5*0 1 32 6*0 1 1 32 5*0 1 32 6*0 32 7*0 32 7*0 1 1 32 5*0 5 9 32 5*0
  //   32 7*0 32
  //   contents of rom_3 (hex, n*v repeats v):
  //   32*0 2 8*0 40 80 6*0 40 80 6*0 10 6*0 20 24*0 10 6*0 20 16*0 10 6*0 4 7*0 42 9 4 1 4*0 1 7*0 1 7*0 1
  //   7*0 1 7*0 1 7*0 20 20 20 6*0 10 6*0 2 2 2 6*0 1 6*0 10 7*0 6 7*0 42 9 4
  //   contents of rom_4 (hex, n*v repeats v):
  //   43*0 1 7*0 1 68*0 10 9*0 8 2 4*0 8 7*0 c 7*0 40 7*0 80 7*0 20 57*0 2
  //   contents of rom_5 (hex, n*v repeats v):
  //   5*0 40 0 0 1 7*0 4 0 0 2 0 1 0 0 8 8 79*0 8 88 8 4*0 8 8 62*0 8 88 8 5*0 8 8 6*0 10 90 10 5*0 10 10
  //   6*0 20
  //   contents of rom_6 (hex, n*v repeats v):
  //   70 94 10 70 94 10 10*0 70 94 10 70 94 10 0 0 1 1 14*0 c0 c8 8 5*0 c0 c8 8 5*0 c0 8 6*0 70 94 10 5*0
  //   80 7*0 80 7*0 40 8 6*0 70 14 10 5*0 c0 a a a 4*0 71 95 10 61*0 2 2 2 5*0 1 1 6*0 2 2 2 5*0 1 1
  //   contents of rom_7 (hex, n*v repeats v):
  //   84 1 0 44 1 0 20 9*0 4 1 0 4 1 19*0 a a 6*0 1a a 6*0 a 7*0 4 1 14*0 8 7*0 8 7*0 8 7*0 a 7*0 4 1
endmodule

module BitTest (
  input  [7:0] DBus_In,
  input  TestFor_1_0,
  input  [2:0] Bit,
  output Conditional_Affirmative
);

  wire [7:0] xnor_1_out;

  Pull_Resistor pull_resistor_1 (.node(DBus_In));
  assign xnor_1_out = ~(DBus_In ^ {8{TestFor_1_0}});  // XNOR_Gate xnor_1, 8 bits wide
  Multiplexer #(.select(3), .enable("false")) multiplexer_1 (
    .in0(xnor_1_out[0]), .in1(xnor_1_out[1]), .in2(xnor_1_out[2]), .in3(xnor_1_out[3]), .in4(xnor_1_out[4]),
    .in5(xnor_1_out[5]), .in6(xnor_1_out[6]), .in7(xnor_1_out[7]), .out(Conditional_Affirmative), .sel(Bit));
endmodule

module main (
);

  wire bittest_1_conditional_affirmative, breakpoint_1_brkpt_triggered, CLK, clock_1_out,
       clockctrl_1_do_step_3, control_1_int__active, DO_STEP_CLK_out, Do_Step_Inst, DO_STEP_INST_out,
       Inst_Step, INT_EN, Interrupt_out, logic_1_comp_c_out, risingedge_dtct_1_out, RST, STEP_CLK_out,
       systemreg1_1_c_out, systemreg1_1_comp_c_out, systemreg1_1_shiftin;
  wire [2:0] alu_1_c, inst_reg_1_inst_output_2;
  wire [4:0] comparison_1_comparison1;
  wire [6:0] systemreg2_1_ram_page;
  wire [7:0] crossover_1_operandb, CTRLBus0, CTRLBus1, CTRLBus2, CTRLBus3, CTRLBus4, CTRLBus5,
       logic_1_register_b_complement, rega_1_value, regb_1_value, systemreg1_1_dbg, systemreg2_1_dbg,
       systemreg2_1_dbus_out, systemreg3_1_dbg, temp_reg_1_dbg_h, temp_reg_1_dbg_l;
  wire [8:0] control_1_dbg, crossover_1_ramabus_out;
  wire [13:0] iadr_reg_1_iadr, pc_1_pc_val, temp_reg_1_romabus_out;
  wire [14:0] stack_1_dbg;
  wire [15:0] inst_reg_1_inst_output, rom_1_nextinst_out;

  LED RAM_W (.in(CTRLBus3[7]));
  LED RAM_R (.in(CTRLBus4[0]));
  // Probe on temp_reg_1_romabus_out
  LED Conditioan_Affirmative (.in(bittest_1_conditional_affirmative));
  LED Conditional_Inc (.in(CTRLBus0[6]));
  LED Latch (.in(CTRLBus0[7]));
  LED Inc (.in(CTRLBus0[5]));
  // Probe on temp_reg_1_dbg_l
  // Probe on temp_reg_1_dbg_h
  LED LatchH (.in(CTRLBus1[7]));
  LED LatchL (.in(CTRLBus1[6]));
  LED OE_DATAL (.in(CTRLBus2[1]));
  LED OE_ADR (.in(CTRLBus2[0]));
  // Probe on systemreg2_1_dbg
  SystemReg2 systemreg2_1 (
    .DBus_IN(systemreg2_1_dbus_out), .RAM_W_Async(CTRLBus3[7]), .RAM_R_Async(CTRLBus4[0]),
    .RAMABus_IN(crossover_1_ramabus_out), .CLK(CLK), .RESET(RST), .DBus_Out(systemreg2_1_dbus_out),
    .Ram_Page(systemreg2_1_ram_page), .DBG(systemreg2_1_dbg));
  LED RAM_W_2 (.in(CTRLBus3[7]));
  LED RAM_R_2 (.in(CTRLBus4[0]));
  // Probe on systemreg3_1_dbg
  // Probe on pc_1_pc_val
  PC pc_1 (
    .Latch_EN(CTRLBus0[7]), .ROMABus_IN(temp_reg_1_romabus_out), .INC_EN(CTRLBus0[5]), .CLK(CLK),
    .RESET(RST), .PC_VAL(pc_1_pc_val), .CNDT_INC_ENT(CTRLBus0[6]),
    .Conditional_Affirmative(bittest_1_conditional_affirmative));
  Temp_Reg temp_reg_1 (
    .DBUS_In(systemreg2_1_dbus_out), .LATCH_L(CTRLBus1[6]), .LATCH_H(CTRLBus1[7]), .CLK(CLK), .RESET(RST),
    .OE_ADR(CTRLBus2[0]), .OE_DATAL(CTRLBus2[1]), .DBUS_Out(systemreg2_1_dbus_out),
    .ROMABus_Out(temp_reg_1_romabus_out), .DBG_H(temp_reg_1_dbg_h), .DBG_L(temp_reg_1_dbg_l));
  SystemReg3 systemreg3_1 (
    .DBus_IN(systemreg2_1_dbus_out), .RAM_W_Async(CTRLBus3[7]), .RAM_R_Async(CTRLBus4[0]),
    .RAMABus_IN(crossover_1_ramabus_out), .CLK(CLK), .RESET(RST), .INT_EN(INT_EN),
    .DBus_Out(systemreg2_1_dbus_out), .DBG(systemreg3_1_dbg), .Comparison(comparison_1_comparison1),
    .Set_Btn_Flag(risingedge_dtct_1_out));
  LED RAM_W_3 (.in(CTRLBus3[7]));
  LED RAM_R_3 (.in(CTRLBus4[0]));
  LED ALU_OE (.in(CTRLBus2[3]));
  LED Comp_OE (.in(CTRLBus2[4]));
  LED ALU_Comp (.in(CTRLBus2[2]));
  Button Reset (.out(RST));
  Button u_Inst_Step (.out(Inst_Step));
  Button u_DO_STEP_INST (.out(DO_STEP_INST_out));
  LED led_1 (.in(Do_Step_Inst));
  IAdr_Reg iadr_reg_1 (.ROMA_IN(pc_1_pc_val), .LATCH_EN(CTRLBus0[4]), .CLK(CLK), .RESET(RST), .IAdr(iadr_reg_1_iadr));
  ROM rom_1 (.PC_VAL_IN(pc_1_pc_val), .NextInst_OUT(rom_1_nextinst_out));
  LED Latch_EN (.in(CTRLBus0[4]));
  LED RAM_Sync_DA (.in(CTRLBus4[1]));
  LED RAM_R_Sync_A (.in(CTRLBus4[0]));
  LED RAM_W_4 (.in(CTRLBus3[7]));
  // Probe on {inst_reg_1_inst_output[15:12], inst_reg_1_inst_output_2, inst_reg_1_inst_output[8:0]}
  Inst_Reg inst_reg_1 (
    .NextInst_Input(rom_1_nextinst_out), .LATCH_EN(CTRLBus0[4]), .CLK(CLK), .RESET(RST),
    .Inst_Output({inst_reg_1_inst_output[15:12], inst_reg_1_inst_output_2, inst_reg_1_inst_output[8:0]}));
  // Probe on systemreg1_1_dbg
  SystemReg1 systemreg1_1 (
    .DBus_IN(systemreg2_1_dbus_out), .RAM_W_Async(CTRLBus3[7]), .RAM_R_ASync(CTRLBus4[0]),
    .ALU_OE(CTRLBus2[3]), .RAMABus_IN(crossover_1_ramabus_out), .OVF_in(alu_1_c[2]), .HC_in(alu_1_c[1]),
    .C_in(alu_1_c[0]), .CLK(CLK), .ShiftIn(systemreg1_1_shiftin), .DBus_OUT(systemreg2_1_dbus_out),
    .DBG(systemreg1_1_dbg), .RESET(RST), .C_out(systemreg1_1_c_out), .COMP_C_in(logic_1_comp_c_out),
    .Comp_C_Out(systemreg1_1_comp_c_out), .Comp_OE(CTRLBus2[4]), .ALU_Comp_B(CTRLBus2[2]));
  RAM ram_1 (
    .RAMABus_In(crossover_1_ramabus_out), .DBus_In(systemreg2_1_dbus_out), .RESET(RST),
    .Async_W(CTRLBus3[7]), .AsyncR_LatchSafeA(CTRLBus4[0]), .DBus_Out(systemreg2_1_dbus_out),
    .Page_in(systemreg2_1_ram_page), .LatchSafeDA(CTRLBus4[1]), .Clk(CLK));
  LED IAdr_L____DBus (.in(CTRLBus5[6]));
  LED RegB____RAMA_L (.in(CTRLBus3[4]));
  LED In____DBus (.in(CTRLBus3[5]));
  LED Int_Adr__ROMA (.in(CTRLBus3[6]));
  T_Flip_Flop t_ff_1 (.clk(DO_STEP_INST_out), .T(1'b1), .Q(Do_Step_Inst));  // open: Qn, preset, reset, en
  BreakPoint breakpoint_1 (.ADR(iadr_reg_1_iadr), .BRKPT_Triggered(breakpoint_1_brkpt_triggered));
  Button Interrupt (.out(Interrupt_out));
  // Probe on control_1_dbg
  LED led_2 (.in(control_1_int__active));
  Control control_1 (
    .CLK(CLK), .RESET(RST), .CTRL_BUS_0(CTRLBus0),
    .INST({inst_reg_1_inst_output[15:12], inst_reg_1_inst_output_2, inst_reg_1_inst_output[8:0]}),
    .CTRL_BUS_1(CTRLBus1), .CTRL_BUS_2(CTRLBus2), .CTRL_BUS_3(CTRLBus3), .CTRL_BUS_4(CTRLBus4),
    .DBG(control_1_dbg), .INT_EN(INT_EN), .INT(risingedge_dtct_1_out), .Int__Active(control_1_int__active),
    .CTRL_BUS_5(CTRLBus5), .BreakPoint(breakpoint_1_brkpt_triggered), .DO_STEP_INST(Do_Step_Inst),
    .STEP_INST(Inst_Step));
  BitTest bittest_1 (
    .DBus_In(systemreg2_1_dbus_out), .TestFor_1_0(inst_reg_1_inst_output[12]),
    .Bit(inst_reg_1_inst_output_2), .Conditional_Affirmative(bittest_1_conditional_affirmative));
  LED IAdr_H____DBus (.in(CTRLBus5[7]));
  LED In__ROMA (.in(CTRLBus3[0]));
  LED PC_L____DBus (.in(CTRLBus3[1]));
  LED PC_H____DBus (.in(CTRLBus3[2]));
  LED In____RAMA_L (.in(CTRLBus3[3]));
  CrossOver crossover_1 (
    .Inst({inst_reg_1_inst_output[15:12], inst_reg_1_inst_output_2, inst_reg_1_inst_output[8:0]}),
    .PC_Val(pc_1_pc_val), .RegB(regb_1_value), .Inst_0__13___ROMABus(CTRLBus3[0]),
    .PC_Val_0__7___DBus(CTRLBus3[1]), .PC_Val_8__13___DBus(CTRLBus3[2]),
    .Inst_0__8___RAMABus_0__8(CTRLBus3[3]), .Inst_0__8__RegB__RAMABus_0__8(CTRLBus3[4]),
    .ROMABus_Out(temp_reg_1_romabus_out), .RAMABus_Out(crossover_1_ramabus_out),
    .DBus_Out(systemreg2_1_dbus_out), .OperandB(crossover_1_operandb), .Inst_0__7___DBus(CTRLBus3[5]),
    .INTAdr__ROMA(CTRLBus3[6]), .Inst_Adr(iadr_reg_1_iadr), .InstAdr_0__7___DBus(CTRLBus5[6]),
    .InstAdr_8__13___DBus(CTRLBus5[7]));
  RisingEdge_Dtct risingedge_dtct_1 (.CLK(CLK), .IN(Interrupt_out), .RESET(1'b0), .OUT(risingedge_dtct_1_out));
  LED W (.in(CTRLBus4[2]));
  LED Ptr_L (.in(CTRLBus4[7]));
  LED R (.in(CTRLBus4[3]));
  LED Of_1 (.in(CTRLBus5[0]));
  LED PresD (.in(CTRLBus4[4]));
  LED Of__1 (.in(CTRLBus5[1]));
  LED SyncD (.in(CTRLBus4[5]));
  LED Of_0 (.in(CTRLBus5[2]));
  LED SyncA (.in(CTRLBus4[6]));
  LED OE (.in(CTRLBus2[3]));
  LED B_Comp (.in(CTRLBus2[2]));
  LED Comp_B (.in(CTRLBus2[4]));
  LED Dual_OE (.in(CTRLBus2[6]));
  LED Not_A (.in(CTRLBus2[5]));
  LED DirR (.in(inst_reg_1_inst_output[7]));
  LED ShiftIn (.in(systemreg1_1_shiftin));
  LED OE_2 (.in(CTRLBus2[7]));
  // Probe on stack_1_dbg
  ALU alu_1 (
    .Register_A(rega_1_value), .Operand_B(crossover_1_operandb), .Do_B_Komp(CTRLBus2[2]), .OE(CTRLBus2[3]),
    .DBus_OUT(systemreg2_1_dbus_out), .RegB_Komplement(logic_1_register_b_complement), .HC(alu_1_c[1]),
    .C(alu_1_c[0]), .OVF(alu_1_c[2]), .DO_C_in(inst_reg_1_inst_output_2[2]), .C_in(systemreg1_1_c_out));
  Logic logic_1 (
    .COMP(CTRLBus2[4]), .NOT(CTRLBus2[5]), .DUAL_OP_OE(CTRLBus2[6]), .Register_A(rega_1_value),
    .Operand_B(crossover_1_operandb), .DBus_Out(systemreg2_1_dbus_out),
    .Register_B_Complement(logic_1_register_b_complement),
    .Inst({inst_reg_1_inst_output[15:12], inst_reg_1_inst_output_2, inst_reg_1_inst_output[8:0]}),
    .COMP_C_IN(systemreg1_1_comp_c_out), .COMP_C_OUT(logic_1_comp_c_out));
  BarrelShifter barrelshifter_1 (
    .Register_A(rega_1_value), .R(inst_reg_1_inst_output[7]), .DBus_OUT(systemreg2_1_dbus_out),
    .Operand_B(crossover_1_operandb), .OE(CTRLBus2[7]), .Shift_In(systemreg1_1_shiftin));
  Stack stack_1 (
    .DATABUS_IN(systemreg2_1_dbus_out), .Present_Data(CTRLBus4[4]), .CLK(CLK), .RESET(RST), .R(CTRLBus4[3]),
    .W(CTRLBus4[2]), .DATABUS_OUT(systemreg2_1_dbus_out), .DBG(stack_1_dbg), .Sync_Data(CTRLBus4[5]),
    .Ptr_Latch(CTRLBus4[7]), .Ofs_Sgn(CTRLBus5[3]), .Ofs_1(CTRLBus5[0]), .Ofs__1(CTRLBus5[1]),
    .Inst({inst_reg_1_inst_output[15:12], inst_reg_1_inst_output_2, inst_reg_1_inst_output[8:0]}),
    .Sync_Adr(CTRLBus4[6]), .Ofs_0(CTRLBus5[2]));
  LED Sgn (.in(CTRLBus5[3]));
  Button DO_STEP_CLK (.out(DO_STEP_CLK_out));
  Button STEP_CLK (.out(STEP_CLK_out));
  LED Latch_2 (.in(CTRLBus1[0]));
  LED OE_3 (.in(CTRLBus1[1]));
  LED Latch_3 (.in(CTRLBus1[2]));
  LED OE_4 (.in(CTRLBus1[3]));
  Clock clock_1 (.out(clock_1_out));
  LED led_3 (.in(clockctrl_1_do_step_3));
  // Probe on systemreg2_1_dbus_out
  // Probe on rega_1_value
  RegA rega_1 (
    .DBus_IN(systemreg2_1_dbus_out), .LATCH_EN(CTRLBus1[0]), .CLK(CLK), .RESET(RST), .OE(CTRLBus1[1]),
    .DBus_Out(systemreg2_1_dbus_out), .Value(rega_1_value));
  // Probe on regb_1_value
  RegB regb_1 (
    .DBus_IN(systemreg2_1_dbus_out), .LATCH_EN(CTRLBus1[2]), .CLK(CLK), .RESET(RST), .OE(CTRLBus1[3]),
    .DBus_Out(systemreg2_1_dbus_out), .Value(regb_1_value));
  ClockCTRL clockctrl_1 (
    .MCLOCK_IN(clock_1_out), .Do_Step(DO_STEP_CLK_out), .Do_Step_3(clockctrl_1_do_step_3),
    .Do_Step_2(STEP_CLK_out), .CLK(CLK), .Reset(RST));
  Comparison comparison_1 (.A(rega_1_value), .B(regb_1_value), .Comparison1(comparison_1_comparison1));

  // Notes on the sheet:
  //   ROMABus:
  //   (hex)
  //   H
  //   L
  //   (hex)
  //   Val:
  //   (hex)
  //   Val:
  //   (hex)
  //   PC Val:
  //   (hex)
  //   Val:
  //   (hex)
  //   Current Inst:
  //   (hex)
  //   InstCode+Step:
  //   Val:
  //   (hex)
  //   Val:
  //   (hex)
  //   Val:
  //   (hex)
  //   Data Bus
  //   (hex)
endmodule

// CLK
module ClockCTRL (
  input  MCLOCK_IN,
  input  Do_Step,
  input  Do_Step_2,
  input  Reset,
  output CLK,
  output Do_Step_3
);

  wire and_1_out, d_ff_1_q, d_ff_1_qn, not_1_out, not_2_out, t_ff_1_qn, t_ff_2_q;

  T_Flip_Flop t_ff_1 (.clk(Do_Step), .T(1'b1), .Q(Do_Step_3), .Qn(t_ff_1_qn));  // open: preset, reset, en
  not not_1 (not_1_out, MCLOCK_IN);
  D_Flip_Flop d_ff_1 (
    .clk(not_1_out), .D(t_ff_1_qn), .Q(d_ff_1_q), .Qn(d_ff_1_qn), .en(not_2_out), .reset(Reset));  // open: preset
  T_Flip_Flop t_ff_2 (.clk(MCLOCK_IN), .T(d_ff_1_q), .Q(t_ff_2_q), .reset(Reset));  // open: Qn, preset, en
  not not_2 (not_2_out, t_ff_2_q);
  and and_1 (and_1_out, d_ff_1_qn, Do_Step_2);
  or or_1 (CLK, t_ff_2_q, and_1_out);
endmodule

module BreakPoint (
  input  [13:0] ADR,
  output BRKPT_Triggered
);

  wire and_1_out, and_2_out, rom_adr_test_1_out_3, rom_adr_test_2_out_3;

  ROM_Adr_Test rom_adr_test_1 (.Address_Is(14'h6), .Address_Should(ADR), .out_3(rom_adr_test_1_out_3));
  ROM_Adr_Test rom_adr_test_2 (.Address_Is(14'h9), .Address_Should(ADR), .out_3(rom_adr_test_2_out_3));
  and and_1 (and_1_out, rom_adr_test_1_out_3, 1'b0);
  and and_2 (and_2_out, rom_adr_test_2_out_3, 1'b0);
  or or_1 (BRKPT_Triggered, and_1_out, and_2_out);

  // Notes on the sheet:
  //   Break at adr:
  //   Enable Breakpoint:
  //   Break at adr:
  //   Enable Breakpoint:
endmodule

module ROM_Adr_Test (
  input  [13:0] Address_Is,
  input  [13:0] Address_Should,
  output out_3
);

  wire [13:0] xnor_1_out;

  Pull_Resistor pull_resistor_1 (.node(Address_Is));
  assign xnor_1_out = ~(Address_Is ^ Address_Should);  // XNOR_Gate xnor_1, 14 bits wide
  // Probe on xnor_1_out
  and and_1 (out_3, xnor_1_out[0], xnor_1_out[1], xnor_1_out[2], xnor_1_out[3], xnor_1_out[4], xnor_1_out[5], xnor_1_out[6], xnor_1_out[7], xnor_1_out[8], xnor_1_out[9], xnor_1_out[10], xnor_1_out[11], xnor_1_out[12], xnor_1_out[13]);
endmodule

module ScratchRegs (
  input  [7:0] DBus_IN,
  input  RAM_W_Async,
  input  RAM_R_ASync,
  input  [8:0] RAMABus_IN,
  input  CLK,
  input  RESET,
  output [7:0] DBus_OUT
);

  wire adr_test_1_out_3, adr_test_2_out_3, adr_test_3_out_3, adr_test_4_out_3, and_1_out, and_2_out,
       and_3_out, and_4_out, and_5_out, and_6_out, and_7_out, and_8_out, and_9_out, or_1_out;
  wire [7:0] rega_1_dbus_out;

  Adr_Test adr_test_1 (.Address_Is(RAMABus_IN), .Address_Should(9'h100), .out_3(adr_test_1_out_3));
  Adr_Test adr_test_2 (.Address_Is(RAMABus_IN), .Address_Should(9'h101), .out_3(adr_test_2_out_3));
  Adr_Test adr_test_3 (.Address_Is(RAMABus_IN), .Address_Should(9'h102), .out_3(adr_test_3_out_3));
  Adr_Test adr_test_4 (.Address_Is(RAMABus_IN), .Address_Should(9'h103), .out_3(adr_test_4_out_3));
  or or_1 (or_1_out, adr_test_1_out_3, adr_test_2_out_3, adr_test_3_out_3, adr_test_4_out_3);
  and and_1 (and_1_out, RAM_W_Async, adr_test_1_out_3);
  and and_2 (and_2_out, RAM_R_ASync, adr_test_1_out_3);
  and and_3 (and_3_out, RAM_W_Async, adr_test_2_out_3);
  and and_4 (and_4_out, RAM_R_ASync, adr_test_2_out_3);
  and and_5 (and_5_out, RAM_W_Async, adr_test_3_out_3);
  and and_6 (and_6_out, RAM_R_ASync, adr_test_3_out_3);
  and and_7 (and_7_out, RAM_W_Async, adr_test_4_out_3);
  and and_8 (and_8_out, RAM_R_ASync, adr_test_4_out_3);
  and and_9 (and_9_out, or_1_out, RAM_R_ASync);
  RegA rega_1 (
    .DBus_IN(DBus_IN), .LATCH_EN(and_1_out), .CLK(CLK), .RESET(RESET), .OE(and_2_out),
    .DBus_Out(rega_1_dbus_out));  // open: Value
  RegA rega_2 (
    .DBus_IN(DBus_IN), .LATCH_EN(and_3_out), .CLK(CLK), .RESET(RESET), .OE(and_4_out),
    .DBus_Out(rega_1_dbus_out));  // open: Value
  RegA rega_3 (
    .DBus_IN(DBus_IN), .LATCH_EN(and_5_out), .CLK(CLK), .RESET(RESET), .OE(and_6_out),
    .DBus_Out(rega_1_dbus_out));  // open: Value
  RegA rega_4 (
    .DBus_IN(DBus_IN), .LATCH_EN(and_7_out), .CLK(CLK), .RESET(RESET), .OE(and_8_out),
    .DBus_Out(rega_1_dbus_out));  // open: Value
  assign DBus_OUT = and_9_out ? rega_1_dbus_out : 8'bz;  // Controlled_Buffer controlled_buffer_1
endmodule

module Halt_Control (
  input  Bkpt,
  input  Step_EN,
  input  SubInst_0,
  input  Halt_Set,
  input  Halt_Clr,
  input  Step,
  input  CLK,
  input  RESET,
  output Halted
);

  wire and_1_out, or_1_out, or_2_out, risingedge_dtct_1_out, s_r_ff_1_q;

  or or_1 (or_1_out, Bkpt, Step_EN);
  S_R_Flip_Flop s_r_ff_1 (
    .S(Halt_Set), .clk(CLK), .R(Halt_Clr), .Q(s_r_ff_1_q), .reset(RESET));  // open: Qn, preset, en
  RisingEdge_Dtct risingedge_dtct_1 (.CLK(CLK), .IN(Step), .RESET(RESET), .OUT(risingedge_dtct_1_out));
  and and_1 (and_1_out, or_1_out, SubInst_0);
  or or_2 (or_2_out, and_1_out, s_r_ff_1_q);
  and and_2 (Halted, or_2_out, ~risingedge_dtct_1_out);  // AND_Gate
endmodule

module Interrupt_Control (
  input  Assert,
  input  Int__Enabled,
  input  InstR_Latch,
  input  Int__Override_Clr,
  input  Int__Clr,
  input  Clk,
  input  Reset,
  output Int_nOverride,
  output Int_Active
);

  wire and_1_out, sr_ff_clrpriority_1_out_5;

  SR_FF_ClrPriority sr_ff_clrpriority_1 (
    .Set(Assert), .Clk(Clk), .Reset(and_1_out), .Async_0(Reset), .out_5(sr_ff_clrpriority_1_out_5));
  and and_1 (and_1_out, sr_ff_clrpriority_1_out_5, Int__Enabled, InstR_Latch, ~Int_Active);  // AND_Gate
  SR_FF_ClrPriority sr_ff_clrpriority_2 (
    .Set(and_1_out), .Clk(Clk), .Reset(Int__Override_Clr), .Async_0(Reset), .out_5(Int_nOverride));
  SR_FF_ClrPriority sr_ff_clrpriority_3 (
    .Set(and_1_out), .Clk(Clk), .Reset(Int__Clr), .Async_0(Reset), .out_5(Int_Active));

  // Other names for the same wires on the sheet: R = Reset

  // Notes on the sheet:
  //   Int Asserted FF
  //   Int Override FF
  //   Int Active FF
endmodule

module SR_FF_ClrPriority (
  input  Set,
  input  Clk,
  input  Reset,
  input  Async_0,
  output out_5
);

  wire and_1_out, or_1_out;

  or or_1 (or_1_out, out_5, Set);
  and and_1 (and_1_out, or_1_out, ~Reset);  // AND_Gate
  D_Flip_Flop d_ff_1 (.clk(Clk), .D(and_1_out), .Q(out_5), .reset(Async_0));  // open: Qn, preset, en
endmodule

module RisingEdge_Dtct (
  input  CLK,
  input  IN,
  input  RESET,
  output OUT
);

  wire d_ff_1_q, d_ff_2_q;

  D_Flip_Flop d_ff_1 (.clk(CLK), .D(IN), .Q(d_ff_1_q), .reset(RESET));  // open: Qn, preset, en
  D_Flip_Flop d_ff_2 (.clk(CLK), .D(d_ff_1_q), .Q(d_ff_2_q), .reset(RESET));  // open: Qn, preset, en
  and and_1 (OUT, ~d_ff_2_q, d_ff_1_q);  // AND_Gate
endmodule

module RegAB_Switch (
  input  [7:0] Bus_In,
  input  [15:0] Inst,
  output [7:0] Bus_Out
);

  wire demultiplexer_1_out0, demultiplexer_1_out1, demultiplexer_2_out0, demultiplexer_2_out1;

  Demultiplexer #(.enable("false")) demultiplexer_1 (
    .out0(demultiplexer_1_out0), .out1(demultiplexer_1_out1), .in(Bus_In[4]), .sel(Inst[9]));
  Demultiplexer #(.enable("false")) demultiplexer_2 (
    .out0(demultiplexer_2_out0), .out1(demultiplexer_2_out1), .in(Bus_In[5]), .sel(Inst[9]));
  or or_1 (Bus_Out[0], Bus_In[0], demultiplexer_1_out0);
  or or_2 (Bus_Out[1], Bus_In[1], demultiplexer_2_out0);
  or or_3 (Bus_Out[2], Bus_In[2], demultiplexer_1_out1);
  or or_4 (Bus_Out[3], Bus_In[3], demultiplexer_2_out1);

  assign Bus_Out[7:4] = {Bus_In[7:6], 2'b00};
endmodule

module IAdr_Reg (
  input  [13:0] ROMA_IN,
  input  LATCH_EN,
  input  CLK,
  input  RESET,
  output [13:0] IAdr
);

  Register #(.width(14)) register_1 (.D(ROMA_IN), .en(LATCH_EN), .Q(IAdr), .clk(CLK), .clr(RESET));
endmodule
